// Logisim project Project-Part-1-3bit-Opcode-ALU-Rtype-Instructions.circ as structural Verilog
// Register File(32*32)
module _32_Bit_Register_File (
  input  [4:0] Read_Register_1__RS,
  input  [4:0] Write_Data__RD,
  input  [4:0] Read_Register_2__RT,
  input  [31:0] WriteData,
  input  RegWrite,
  input  CLK,
  input  Clear,
  output [31:0] Read_Data_1,
  output [31:0] Read_Data_2
);

  wire and_1_out, and_2_out, and_3_out, and_4_out, and_5_out, and_6_out, and_7_out, and_8_out, and_9_out,
       and_10_out, and_11_out, and_12_out, and_13_out, and_14_out, and_15_out, and_16_out, and_17_out,
       and_18_out, and_19_out, and_20_out, and_21_out, and_22_out, and_23_out, and_24_out, and_25_out,
       and_26_out, and_27_out, and_28_out, and_29_out, and_30_out, and_31_out, and_32_out, decoder_1_out0,
       decoder_1_out1, decoder_1_out2, decoder_1_out3, decoder_1_out4, decoder_1_out5, decoder_1_out6,
       decoder_1_out7, decoder_1_out8, decoder_1_out9, decoder_1_out10, decoder_1_out11, decoder_1_out12,
       decoder_1_out13, decoder_1_out14, decoder_1_out15, decoder_1_out16, decoder_1_out17, decoder_1_out18,
       decoder_1_out19, decoder_1_out20, decoder_1_out21, decoder_1_out22, decoder_1_out23, decoder_1_out24,
       decoder_1_out25, decoder_1_out26, decoder_1_out27, decoder_1_out28, decoder_1_out29, decoder_1_out30,
       decoder_1_out31;
  wire [31:0] _0__zero_q, _1__at_q, _2__v0_q, _3__v1_q, _4__a0_q, _5__a1_q, _6__a2_q, _7__a3_q, _8__t0_q,
       _9__t1_q, _10__t2_q, _11__t3_q, _12__t4_q, _13__t5_q, _14__t6_q, _15__t7_q, _16__s0_q, _17__s1_q,
       _18__s2_q, _19__s3_q, _20__s4_q, _21__s5_q, _22__s6_q, _23__s7_q, _24__t8_q, _25__t9_q, _26__k0_q,
       _27__k1_q, _28__gp_q, _29__sp_q, _30__fp_q, _31__ra_q;

  Decoder #(.select(5), .enable("false")) decoder_1 (
    .out0(decoder_1_out0), .out1(decoder_1_out1), .out2(decoder_1_out2), .out3(decoder_1_out3),
    .out4(decoder_1_out4), .out5(decoder_1_out5), .out6(decoder_1_out6), .out7(decoder_1_out7),
    .out8(decoder_1_out8), .out9(decoder_1_out9), .out10(decoder_1_out10), .out11(decoder_1_out11),
    .out12(decoder_1_out12), .out13(decoder_1_out13), .out14(decoder_1_out14), .out15(decoder_1_out15),
    .out16(decoder_1_out16), .out17(decoder_1_out17), .out18(decoder_1_out18), .out19(decoder_1_out19),
    .out20(decoder_1_out20), .out21(decoder_1_out21), .out22(decoder_1_out22), .out23(decoder_1_out23),
    .out24(decoder_1_out24), .out25(decoder_1_out25), .out26(decoder_1_out26), .out27(decoder_1_out27),
    .out28(decoder_1_out28), .out29(decoder_1_out29), .out30(decoder_1_out30), .out31(decoder_1_out31),
    .sel(Write_Data__RD));
  and and_1 (and_1_out, RegWrite, decoder_1_out0);
  and and_2 (and_2_out, RegWrite, decoder_1_out1);
  and and_3 (and_3_out, RegWrite, decoder_1_out2);
  and and_4 (and_4_out, RegWrite, decoder_1_out3);
  and and_5 (and_5_out, RegWrite, decoder_1_out4);
  and and_6 (and_6_out, RegWrite, decoder_1_out5);
  and and_7 (and_7_out, RegWrite, decoder_1_out6);
  and and_8 (and_8_out, RegWrite, decoder_1_out7);
  and and_9 (and_9_out, RegWrite, decoder_1_out8);
  and and_10 (and_10_out, RegWrite, decoder_1_out9);
  and and_11 (and_11_out, RegWrite, decoder_1_out10);
  and and_12 (and_12_out, RegWrite, decoder_1_out11);
  and and_13 (and_13_out, RegWrite, decoder_1_out12);
  and and_14 (and_14_out, RegWrite, decoder_1_out13);
  and and_15 (and_15_out, RegWrite, decoder_1_out14);
  and and_16 (and_16_out, RegWrite, decoder_1_out15);
  and and_17 (and_17_out, RegWrite, decoder_1_out16);
  and and_18 (and_18_out, RegWrite, decoder_1_out17);
  and and_19 (and_19_out, RegWrite, decoder_1_out18);
  and and_20 (and_20_out, RegWrite, decoder_1_out19);
  and and_21 (and_21_out, RegWrite, decoder_1_out20);
  and and_22 (and_22_out, RegWrite, decoder_1_out21);
  and and_23 (and_23_out, RegWrite, decoder_1_out22);
  and and_24 (and_24_out, RegWrite, decoder_1_out23);
  and and_25 (and_25_out, RegWrite, decoder_1_out24);
  and and_26 (and_26_out, RegWrite, decoder_1_out25);
  and and_27 (and_27_out, RegWrite, decoder_1_out26);
  and and_28 (and_28_out, RegWrite, decoder_1_out27);
  and and_29 (and_29_out, RegWrite, decoder_1_out28);
  and and_30 (and_30_out, RegWrite, decoder_1_out29);
  and and_31 (and_31_out, RegWrite, decoder_1_out30);
  and and_32 (and_32_out, RegWrite, decoder_1_out31);
  Register #(.width(32)) _0__zero (.D(WriteData), .en(and_1_out), .Q(_0__zero_q), .clk(CLK), .clr(Clear));
  Register #(.width(32)) _1__at (.D(WriteData), .en(and_2_out), .Q(_1__at_q), .clk(CLK), .clr(Clear));
  Register #(.width(32)) _2__v0 (.D(WriteData), .en(and_3_out), .Q(_2__v0_q), .clk(CLK), .clr(Clear));
  Register #(.width(32)) _3__v1 (.D(WriteData), .en(and_4_out), .Q(_3__v1_q), .clk(CLK), .clr(Clear));
  Register #(.width(32)) _4__a0 (.D(WriteData), .en(and_5_out), .Q(_4__a0_q), .clk(CLK), .clr(Clear));
  Register #(.width(32)) _5__a1 (.D(WriteData), .en(and_6_out), .Q(_5__a1_q), .clk(CLK), .clr(Clear));
  Register #(.width(32)) _6__a2 (.D(WriteData), .en(and_7_out), .Q(_6__a2_q), .clk(CLK), .clr(Clear));
  Register #(.width(32)) _7__a3 (.D(WriteData), .en(and_8_out), .Q(_7__a3_q), .clk(CLK), .clr(Clear));
  Register #(.width(32)) _8__t0 (.D(WriteData), .en(and_9_out), .Q(_8__t0_q), .clk(CLK), .clr(Clear));
  Register #(.width(32)) _9__t1 (.D(WriteData), .en(and_10_out), .Q(_9__t1_q), .clk(CLK), .clr(Clear));
  Register #(.width(32)) _10__t2 (.D(WriteData), .en(and_11_out), .Q(_10__t2_q), .clk(CLK), .clr(Clear));
  Register #(.width(32)) _11__t3 (.D(WriteData), .en(and_12_out), .Q(_11__t3_q), .clk(CLK), .clr(Clear));
  Register #(.width(32)) _12__t4 (.D(WriteData), .en(and_13_out), .Q(_12__t4_q), .clk(CLK), .clr(Clear));
  Register #(.width(32)) _13__t5 (.D(WriteData), .en(and_14_out), .Q(_13__t5_q), .clk(CLK), .clr(Clear));
  Register #(.width(32)) _14__t6 (.D(WriteData), .en(and_15_out), .Q(_14__t6_q), .clk(CLK), .clr(Clear));
  Register #(.width(32)) _15__t7 (.D(WriteData), .en(and_16_out), .Q(_15__t7_q), .clk(CLK), .clr(Clear));
  Register #(.width(32)) _16__s0 (.D(WriteData), .en(and_17_out), .Q(_16__s0_q), .clk(CLK), .clr(Clear));
  Register #(.width(32)) _17__s1 (.D(WriteData), .en(and_18_out), .Q(_17__s1_q), .clk(CLK), .clr(Clear));
  Register #(.width(32)) _18__s2 (.D(WriteData), .en(and_19_out), .Q(_18__s2_q), .clk(CLK), .clr(Clear));
  Register #(.width(32)) _19__s3 (.D(WriteData), .en(and_20_out), .Q(_19__s3_q), .clk(CLK), .clr(Clear));
  Register #(.width(32)) _20__s4 (.D(WriteData), .en(and_21_out), .Q(_20__s4_q), .clk(CLK), .clr(Clear));
  Register #(.width(32)) _21__s5 (.D(WriteData), .en(and_22_out), .Q(_21__s5_q), .clk(CLK), .clr(Clear));
  Register #(.width(32)) _22__s6 (.D(WriteData), .en(and_23_out), .Q(_22__s6_q), .clk(CLK), .clr(Clear));
  Register #(.width(32)) _23__s7 (.D(WriteData), .en(and_24_out), .Q(_23__s7_q), .clk(CLK), .clr(Clear));
  Register #(.width(32)) _24__t8 (.D(WriteData), .en(and_25_out), .Q(_24__t8_q), .clk(CLK), .clr(Clear));
  Register #(.width(32)) _25__t9 (.D(WriteData), .en(and_26_out), .Q(_25__t9_q), .clk(CLK), .clr(Clear));
  Register #(.width(32)) _26__k0 (.D(WriteData), .en(and_27_out), .Q(_26__k0_q), .clk(CLK), .clr(Clear));
  Register #(.width(32)) _27__k1 (.D(WriteData), .en(and_28_out), .Q(_27__k1_q), .clk(CLK), .clr(Clear));
  Register #(.width(32)) _28__gp (.D(WriteData), .en(and_29_out), .Q(_28__gp_q), .clk(CLK), .clr(Clear));
  Register #(.width(32)) _29__sp (.D(WriteData), .en(and_30_out), .Q(_29__sp_q), .clk(CLK), .clr(Clear));
  Register #(.width(32)) _30__fp (.D(WriteData), .en(and_31_out), .Q(_30__fp_q), .clk(CLK), .clr(Clear));
  Register #(.width(32)) _31__ra (.D(WriteData), .en(and_32_out), .Q(_31__ra_q), .clk(CLK), .clr(Clear));
  Multiplexer #(.select(5), .width(32), .enable("false")) multiplexer_1 (
    .in0(_0__zero_q), .in1(_1__at_q), .in2(_2__v0_q), .in3(_3__v1_q), .in4(_4__a0_q), .in5(_5__a1_q),
    .in6(_6__a2_q), .in7(_7__a3_q), .in8(_8__t0_q), .in9(_9__t1_q), .in10(_10__t2_q), .in11(_11__t3_q),
    .in12(_12__t4_q), .in13(_13__t5_q), .in14(_14__t6_q), .in15(_15__t7_q), .in16(_16__s0_q),
    .in17(_17__s1_q), .in18(_18__s2_q), .in19(_19__s3_q), .in20(_20__s4_q), .in21(_21__s5_q),
    .in22(_22__s6_q), .in23(_23__s7_q), .in24(_24__t8_q), .in25(_25__t9_q), .in26(_26__k0_q),
    .in27(_27__k1_q), .in28(_28__gp_q), .in29(_29__sp_q), .in30(_30__fp_q), .in31(_31__ra_q),
    .out(Read_Data_1), .sel(Read_Register_1__RS));
  Multiplexer #(.select(5), .width(32), .enable("false")) multiplexer_2 (
    .in0(_0__zero_q), .in1(_1__at_q), .in2(_2__v0_q), .in3(_3__v1_q), .in4(_4__a0_q), .in5(_5__a1_q),
    .in6(_6__a2_q), .in7(_7__a3_q), .in8(_8__t0_q), .in9(_9__t1_q), .in10(_10__t2_q), .in11(_11__t3_q),
    .in12(_12__t4_q), .in13(_13__t5_q), .in14(_14__t6_q), .in15(_15__t7_q), .in16(_16__s0_q),
    .in17(_17__s1_q), .in18(_18__s2_q), .in19(_19__s3_q), .in20(_20__s4_q), .in21(_21__s5_q),
    .in22(_22__s6_q), .in23(_23__s7_q), .in24(_24__t8_q), .in25(_25__t9_q), .in26(_26__k0_q),
    .in27(_27__k1_q), .in28(_28__gp_q), .in29(_29__sp_q), .in30(_30__fp_q), .in31(_31__ra_q),
    .out(Read_Data_2), .sel(Read_Register_2__RT));
endmodule

// IF
module Instruction_Fetch__IF (
  input  CLK,
  input  Clear,
  output [31:0] Data
);

  wire [1:0] adder_1_out, register_1_q;

  Register #(.width(2)) register_1 (.D(adder_1_out), .Q(register_1_q), .clk(CLK), .clr(Clear));  // open: en
  ROM #(.addrWidth(2), .dataWidth(32)) rom_1 (.addr(register_1_q), .data(Data));  // open: sel
  Adder #(.width(2)) adder_1 (.a(register_1_q), .b(2'b01), .out(adder_1_out));  // open: cin, cout

  // Notes on the sheet:
  //   contents of rom_1 (hex, n*v repeats v):
  //   11ee6800 15095000 1a119000 1e74a800
endmodule

// ALU
module _32_Bit_ALU_using_Subtractor___Adder (
  input  [31:0] A,
  input  [31:0] B,
  input  [2:0] Opcode,
  output [31:0] Data
);

  wire [31:0] adder_1_out, and_1_out, divider_1_out, multiplier_1_out, or_1_out, subtractor_1_out,
       xnor_1_out, xor_1_out;

  assign and_1_out = A & B;  // AND_Gate and_1, 32 bits wide
  assign or_1_out = A | B;  // OR_Gate or_1, 32 bits wide
  assign xor_1_out = A ^ B;  // XOR_Gate xor_1, 32 bits wide
  assign xnor_1_out = ~(A ^ B);  // XNOR_Gate xnor_1, 32 bits wide
  Adder #(.width(32)) adder_1 (.a(A), .b(B), .out(adder_1_out));  // open: cin, cout
  Subtractor #(.width(32)) subtractor_1 (.a(A), .b(B), .out(subtractor_1_out));  // open: bin, bout
  Multiplier #(.width(32)) multiplier_1 (.a(A), .b(B), .out(multiplier_1_out));  // open: cin, cout
  Divider #(.width(32)) divider_1 (.a(A), .b(B), .out(divider_1_out));  // open: upper, rem
  Multiplexer #(.select(3), .width(32), .enable("false")) multiplexer_1 (
    .in0(and_1_out), .in1(or_1_out), .in2(xor_1_out), .in3(xnor_1_out), .in4(adder_1_out),
    .in5(subtractor_1_out), .in6(multiplier_1_out), .in7(divider_1_out), .out(Data), .sel(Opcode));
endmodule

module Rtype_Using_3bit_Opcode_ALU (
  input  in_1,
  input  in_2,
  output [5:0] Fnc,
  output [4:0] shamt,
  output [4:0] RT,
  output [4:0] RS,
  output [4:0] RD,
  output [31:0] out_8,
  output [5:0] opcode,
  output [31:0] Data
);

  wire clock_1_out;
  wire [2:0] bit_extender_1_out;
  wire [31:0] n32_bit_register_file_1_read_data_1, n32_bit_register_file_1_read_data_2;

  Clock clock_1 (.out(clock_1_out));
  Instruction_Fetch__IF instruction_fetch_if_1 (.Data({opcode, out_8[25:6], Fnc}), .CLK(clock_1_out), .Clear(in_1));
  _32_Bit_Register_File u_32_bit_register_file_1 (
    .WriteData(Data), .Read_Data_1(n32_bit_register_file_1_read_data_1), .Read_Register_1__RS(out_8[20:16]),
    .Read_Data_2(n32_bit_register_file_1_read_data_2), .Read_Register_2__RT(out_8[15:11]),
    .Write_Data__RD(out_8[25:21]), .RegWrite(in_2), .CLK(clock_1_out), .Clear(in_1));
  Bit_Extender #(.in_width(6), .out_width(3)) bit_extender_1 (.in(opcode), .out(bit_extender_1_out));
  _32_Bit_ALU_using_Subtractor___Adder u_32_bit_alu_using_subtractor_adder_1 (
    .A(n32_bit_register_file_1_read_data_1), .B(n32_bit_register_file_1_read_data_2), .Data(Data),
    .Opcode(bit_extender_1_out));

  assign {out_8[31:26], out_8[5:0]} = {opcode, Fnc};
  assign RD = out_8[25:21];
  assign RS = out_8[20:16];
  assign RT = out_8[15:11];
  assign shamt = out_8[10:6];
endmodule
